# Fritzing sketch simit (saved by Fritzing 0.9.4)
breadboards: 1

parts:
  Part1 = Arduino Uno (Rev3)
  IR1 = TSOP312.., 314.. [package=THT]
  Nokia_5110_LCD_Module1 = Nokia 5110 LCD
  J1 = Piezo Speaker

nets:
  N1: Part1.D10_PWM/SS, J1.pin2
  N2: Part1.D2, IR1.Data
  N3: Part1.D3_PWM, Nokia_5110_LCD_Module1.VCC
  N4: Part1.D4, Nokia_5110_LCD_Module1.GND
  N5: Part1.D5_PWM, Nokia_5110_LCD_Module1.SCE
  N6: Part1.D6_PWM, Nokia_5110_LCD_Module1.RST
  N7: Part1.D7, Nokia_5110_LCD_Module1.D/C
  N8: IR1.GND, Nokia_5110_LCD_Module1.LED, Nokia_5110_LCD_Module1.LED_(out)
  N9: IR1.Vs, Nokia_5110_LCD_Module1.DN(MOSI), Nokia_5110_LCD_Module1.SCLK, Nokia_5110_LCD_Module1.DN(MODI)_(out), J1.pin1

custom parts:
  Nokia 5110 LCD: Nokia 5110 Graphic 84*48 LCD module such as the Sparkfun LCD-10168 or the clones from Ebay. There is example code for the Arduino available from the Sparkfun site in https://learn.sparkfun.com/tutorials/graphic-lcd-hookup-guide This is a 3.3V device, if you are running it from a 5V micro you need a 5V tolorant level translator such as the 74ahc367 to protect the signal imputs. Rafa G. did a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
